// Logisim project 16 bit R-I-Type.circ as structural Verilog: 5 circuits, main circuit main
module main (
  input  [3:0] in_1
);

  wire clock_1_out, control_unit_1_out_2;
  wire [2:0] multiplexer_1_out;
  wire [3:0] adder_1_out, register_1_q;
  wire [15:0] alu_1_out_5, read_and_write_1_rs, read_and_write_1_rt;
  wire [31:0] rom_1_data;

  Clock clock_1 (.out(clock_1_out));
  Adder #(.width(4)) adder_1 (.a(in_1), .b(register_1_q), .out(adder_1_out));  // open: cin, cout
  Register #(.width(4)) register_1 (.D(adder_1_out), .Q(register_1_q), .clk(clock_1_out));  // open: en, clr
  ROM #(.addrWidth(4), .dataWidth(32)) rom_1 (.addr(register_1_q), .data(rom_1_data));  // open: sel
  Multiplexer #(.width(3), .enable("false")) multiplexer_1 (
    .in0(rom_1_data[18:16]), .in1(rom_1_data[13:11]), .out(multiplexer_1_out), .sel(control_unit_1_out_2));
  Control_Unit control_unit_1 (.in_1(rom_1_data[31:26]), .out_2(control_unit_1_out_2));
  ALU alu_1 (
    .rs(read_and_write_1_rs), .rt(read_and_write_1_rt), .out_5(alu_1_out_5), .in_3(rom_1_data[2:0]),
    .in_4(control_unit_1_out_2));
  Data_Memory data_memory_1 (
    .sw_sel(rom_1_data[2:0]), .clk(clock_1_out), .lw_sel(rom_1_data[2:0]));  // open: rd_val, sw_enable, clr, lw_enable, lw_out
  Read_And_Write read_and_write_1 (
    .alu_out(alu_1_out_5), .rd_sel(multiplexer_1_out), .in_5(clock_1_out), .rs_sel(rom_1_data[23:21]),
    .rt_sel(rom_1_data[18:16]), .rs(read_and_write_1_rs), .rt(read_and_write_1_rt));  // open: in_6

  // Notes on the sheet:
  //   contents of rom_1 (hex, n*v repeats v):
  //   c0000000
endmodule

module Control_Unit (
  input  [5:0] in_1,
  output out_2
);

  wire and_1_out, nor_1_out, not_1_out, not_2_out, not_3_out, not_4_out, not_5_out, not_6_out;

  not not_1 (not_1_out, in_1[0]);
  not not_2 (not_2_out, in_1[1]);
  not not_3 (not_3_out, in_1[2]);
  not not_4 (not_4_out, in_1[3]);
  not not_5 (not_5_out, in_1[4]);
  not not_6 (not_6_out, in_1[5]);
  and and_1 (and_1_out, not_1_out, not_2_out, not_3_out, not_4_out, not_5_out, not_6_out);
  nor nor_1 (nor_1_out, in_1[0], in_1[1], in_1[2], in_1[3], in_1[4], in_1[5]);
  or or_1 (out_2, and_1_out, nor_1_out);
endmodule

module ALU (
  input  [15:0] rs,
  input  [15:0] rt,
  input  [2:0] in_3,
  input  in_4,
  output [15:0] out_5
);

  wire [15:0] adder_1_out, and_1_out, divider_1_out, multiplier_1_out, or_1_out, subtractor_1_out, xor_1_out;

  Adder #(.width(16)) adder_1 (.a(rs), .b(rt), .out(adder_1_out));  // open: cin, cout
  Subtractor #(.width(16)) subtractor_1 (.a(rs), .b(rt), .out(subtractor_1_out));  // open: bin, bout
  Multiplier #(.width(16)) multiplier_1 (.a(rs), .b(rt), .out(multiplier_1_out));  // open: cin, cout
  Divider #(.width(16)) divider_1 (.a(rs), .b(rt), .out(divider_1_out));  // open: upper, rem
  assign and_1_out = rs & rt;  // AND_Gate and_1, 16 bits wide
  assign or_1_out = rs | rt;  // OR_Gate or_1, 16 bits wide
  assign xor_1_out = rs ^ rt;  // XOR_Gate xor_1, 16 bits wide
  Multiplexer #(.select(3), .width(16)) multiplexer_1 (
    .in0(adder_1_out), .in1(subtractor_1_out), .in2(multiplier_1_out), .in3(divider_1_out), .in4(and_1_out),
    .in5(or_1_out), .in6(xor_1_out), .out(out_5), .sel(in_3), .en(in_4));  // open: in7
endmodule

module Read_And_Write (
  input  [15:0] alu_out,
  input  [2:0] rs_sel,
  input  [2:0] rd_sel,
  input  [2:0] rt_sel,
  input  in_5,
  input  in_6,
  output [15:0] rs,
  output [15:0] rt
);

  wire decoder_1_out0, decoder_1_out1, decoder_1_out2, decoder_1_out3, decoder_1_out4, decoder_1_out5,
       decoder_1_out6, decoder_1_out7;
  wire [15:0] register_1_q, register_2_q, register_3_q, register_4_q, register_5_q, register_6_q,
       register_7_q, register_8_q;

  Decoder #(.select(3), .enable("false")) decoder_1 (
    .out0(decoder_1_out0), .out1(decoder_1_out1), .out2(decoder_1_out2), .out3(decoder_1_out3),
    .out4(decoder_1_out4), .out5(decoder_1_out5), .out6(decoder_1_out6), .out7(decoder_1_out7), .sel(rd_sel));
  Register #(.width(16)) register_1 (.D(alu_out), .en(decoder_1_out0), .Q(register_1_q), .clk(in_5), .clr(in_6));
  Register #(.width(16)) register_2 (.D(alu_out), .en(decoder_1_out1), .Q(register_2_q), .clk(in_5), .clr(in_6));
  Register #(.width(16)) register_3 (.D(alu_out), .en(decoder_1_out2), .Q(register_3_q), .clk(in_5), .clr(in_6));
  Register #(.width(16)) register_4 (.D(alu_out), .en(decoder_1_out3), .Q(register_4_q), .clk(in_5), .clr(in_6));
  Register #(.width(16)) register_5 (.D(alu_out), .en(decoder_1_out4), .Q(register_5_q), .clk(in_5), .clr(in_6));
  Register #(.width(16)) register_6 (.D(alu_out), .en(decoder_1_out5), .Q(register_6_q), .clk(in_5), .clr(in_6));
  Register #(.width(16)) register_7 (.D(alu_out), .en(decoder_1_out6), .Q(register_7_q), .clk(in_5), .clr(in_6));
  Register #(.width(16)) register_8 (.D(alu_out), .en(decoder_1_out7), .Q(register_8_q), .clk(in_5), .clr(in_6));
  Multiplexer #(.select(3), .width(16), .enable("false")) multiplexer_1 (
    .in0(register_1_q), .in1(register_2_q), .in2(register_3_q), .in3(register_4_q), .in4(register_5_q),
    .in5(register_6_q), .in6(register_7_q), .in7(register_8_q), .out(rs), .sel(rs_sel));
  Multiplexer #(.select(3), .width(16), .enable("false")) multiplexer_2 (
    .in0(register_1_q), .in1(register_2_q), .in2(register_3_q), .in3(register_4_q), .in4(register_5_q),
    .in5(register_6_q), .in6(register_7_q), .in7(register_8_q), .out(rt), .sel(rt_sel));

  // Notes on the sheet:
  //   rs
  //   rt
endmodule

module Data_Memory (
  input  [15:0] rd_val,
  input  sw_enable,
  input  [2:0] sw_sel,
  input  [2:0] lw_sel,
  input  lw_enable,
  input  clk,
  input  clr,
  output [15:0] lw_out
);

  wire decoder_1_out0, decoder_1_out1, decoder_1_out2, decoder_1_out3, decoder_1_out4, decoder_1_out5,
       decoder_1_out6, decoder_1_out7;
  wire [15:0] register_1_q, register_2_q, register_3_q, register_4_q, register_5_q, register_6_q,
       register_7_q, register_8_q;

  Decoder #(.select(3)) decoder_1 (
    .out0(decoder_1_out0), .out1(decoder_1_out1), .out2(decoder_1_out2), .out3(decoder_1_out3),
    .out4(decoder_1_out4), .out5(decoder_1_out5), .out6(decoder_1_out6), .out7(decoder_1_out7), .sel(sw_sel),
    .en(sw_enable));
  Register #(.width(16)) register_1 (.D(rd_val), .en(decoder_1_out0), .Q(register_1_q), .clk(clk), .clr(clr));
  Register #(.width(16)) register_2 (.D(rd_val), .en(decoder_1_out1), .Q(register_2_q), .clk(clk), .clr(clr));
  Register #(.width(16)) register_3 (.D(rd_val), .en(decoder_1_out2), .Q(register_3_q), .clk(clk), .clr(clr));
  Register #(.width(16)) register_4 (.D(rd_val), .en(decoder_1_out3), .Q(register_4_q), .clk(clk), .clr(clr));
  Register #(.width(16)) register_5 (.D(rd_val), .en(decoder_1_out4), .Q(register_5_q), .clk(clk), .clr(clr));
  Register #(.width(16)) register_6 (.D(rd_val), .en(decoder_1_out5), .Q(register_6_q), .clk(clk), .clr(clr));
  Register #(.width(16)) register_7 (.D(rd_val), .en(decoder_1_out6), .Q(register_7_q), .clk(clk), .clr(clr));
  Register #(.width(16)) register_8 (.D(rd_val), .en(decoder_1_out7), .Q(register_8_q), .clk(clk), .clr(clr));
  Multiplexer #(.select(3), .width(16)) multiplexer_1 (
    .in0(register_1_q), .in1(register_2_q), .in2(register_3_q), .in3(register_4_q), .in4(register_5_q),
    .in5(register_6_q), .in6(register_7_q), .in7(register_8_q), .out(lw_out), .sel(lw_sel), .en(lw_enable));
endmodule
